// Logisim project logisim.circ as structural Verilog: 17 circuits, main circuit main
module main (
  input  in_1
);

  wire and_1_out, and_2_out, and_3_out, and_4_out, and_5_out, and_6_out, branch_1_bout, clock_1_out,
       controlunit_1_arithmetic, controlunit_1_b, controlunit_1_immediate, controlunit_1_jumpins,
       controlunit_1_memread, controlunit_1_memwrite, controlunit_1_pcread, controlunit_1_pcwrite,
       controlunit_1_we, nor_1_out, or_1_out, or_2_out, or_3_out, or_4_out;
  wire [1:0] controlunit_1_aluselector;
  wire [2:0] controlunit_1_nzp;
  wire [3:0] controlunit_1_dst, controlunit_1_src1, controlunit_1_src2, multiplexer_1_out, multiplexer_2_out;
  wire [17:0] alu_1_out, controlled_buffer_1_out, controlled_buffer_2_out, controlled_buffer_3_out,
       controlunit_1_immextendedarithmetic, controlunit_1_immextendedb, controlunit_1_jumpextended,
       controlunit_1_ld_st_adress, multiplexer_3_out, multiplexer_4_out, n18bithalfadder_1_s,
       n18bithalfadder_2_s, n18bithalfadder_3_s, ram_1_data, register_1_q, registerfile_1_out_7,
       registerfile_1_out_8, rom_1_data;

  Clock clock_1 (.out(clock_1_out));
  and and_1 (and_1_out, controlunit_1_pcread, clock_1_out);
  Register #(.width(18)) register_1 (
    .D(controlled_buffer_3_out), .Q(register_1_q), .clk(and_1_out), .clr(in_1));  // open: en
  or or_1 (or_1_out, controlunit_1_memwrite, and_2_out, controlunit_1_b);
  Multiplexer #(.width(4), .enable("false")) multiplexer_1 (
    .in0(controlunit_1_src2), .in1(controlunit_1_src1), .out(multiplexer_1_out), .sel(or_1_out));
  ROM #(.addrWidth(18), .dataWidth(18)) rom_1 (.addr(register_1_q), .data(rom_1_data), .sel(1'b1));
  Multiplexer #(.width(4), .enable("false")) multiplexer_2 (
    .in0(controlunit_1_src1), .in1(controlunit_1_dst), .out(multiplexer_2_out), .sel(or_2_out));
  or or_2 (or_2_out, controlunit_1_memwrite, and_2_out, controlunit_1_b);
  ControlUnit controlunit_1 (
    .JumpExtended(controlunit_1_jumpextended), .CU_Input(rom_1_data),
    .LD_ST_Adress(controlunit_1_ld_st_adress), .SRC2(controlunit_1_src2), .SRC1(controlunit_1_src1),
    .DST(controlunit_1_dst), .immExtendedB(controlunit_1_immextendedb),
    .immExtendedArithmetic(controlunit_1_immextendedarithmetic), .immediate(controlunit_1_immediate),
    .clk(clock_1_out), .B(controlunit_1_b), .nzp(controlunit_1_nzp), .PCread(controlunit_1_pcread),
    .WE(controlunit_1_we), .jumpIns(controlunit_1_jumpins), .arithmetic(controlunit_1_arithmetic),
    .ALUselector(controlunit_1_aluselector), .memRead(controlunit_1_memread),
    .memWrite(controlunit_1_memwrite), .PCwrite(controlunit_1_pcwrite));
  and and_2 (and_2_out, controlunit_1_immediate, controlunit_1_arithmetic);
  registerFile registerfile_1 (
    .src1(multiplexer_2_out), .src2(multiplexer_1_out), .in_3(multiplexer_4_out), .dest(controlunit_1_dst),
    .WE(controlunit_1_we), .clk(clock_1_out), .out_7(registerfile_1_out_7), .out_8(registerfile_1_out_8));
  branch branch_1 (
    .nzp(controlunit_1_nzp), .op1(registerfile_1_out_7), .op2(registerfile_1_out_8), .Bout(branch_1_bout));
  _18bitHalfAdder u_18bithalfadder_1 (
    .a(register_1_q), .b(controlunit_1_immextendedb), .s(n18bithalfadder_1_s));  // open: cout
  assign controlled_buffer_1_out = or_3_out ? controlunit_1_ld_st_adress : 18'bz;  // Controlled_Buffer controlled_buffer_1
  or or_3 (or_3_out, controlunit_1_memread, controlunit_1_memwrite);
  Multiplexer #(.width(18), .enable("false")) multiplexer_3 (
    .in0(registerfile_1_out_7), .in1(controlunit_1_immextendedarithmetic), .out(multiplexer_3_out),
    .sel(controlunit_1_immediate));
  Multiplexer #(.width(18), .enable("false")) multiplexer_4 (
    .in0(alu_1_out), .in1(ram_1_data), .out(multiplexer_4_out), .sel(controlunit_1_memread));
  assign controlled_buffer_2_out = branch_1_bout ? n18bithalfadder_1_s : 18'bz;  // Controlled_Buffer controlled_buffer_2
  ALU alu_1 (.r1(multiplexer_3_out), .r2(registerfile_1_out_8), .out(alu_1_out), .select(controlunit_1_aluselector));
  _18bitHalfAdder u_18bithalfadder_2 (
    .a(register_1_q), .b(controlunit_1_jumpextended), .s(n18bithalfadder_2_s));  // open: cout
  and and_3 (and_3_out, controlunit_1_jumpins, controlunit_1_pcwrite);
  assign controlled_buffer_3_out = and_3_out ? n18bithalfadder_2_s : 18'bz;  // Controlled_Buffer controlled_buffer_3
  RAM #(.addrWidth(18), .dataWidth(18), .bus("separate")) ram_1 (
    .addr(controlled_buffer_1_out), .din(registerfile_1_out_7), .data(ram_1_data),
    .str(controlunit_1_memwrite), .sel(1'b1), .clk(clock_1_out), .ld(controlunit_1_memread), .clr(1'b0));
  and and_4 (and_4_out, controlunit_1_pcwrite, branch_1_bout, controlunit_1_b);
  assign controlled_buffer_3_out = and_4_out ? controlled_buffer_2_out : 18'bz;  // Controlled_Buffer controlled_buffer_4
  _18bitHalfAdder u_18bithalfadder_3 (.a(register_1_q), .b(18'h1), .s(n18bithalfadder_3_s));  // open: cout
  nor nor_1 (nor_1_out, controlunit_1_jumpins, controlunit_1_b);
  and and_5 (and_5_out, nor_1_out, controlunit_1_pcwrite);
  or or_4 (or_4_out, and_5_out, and_6_out);
  assign controlled_buffer_3_out = or_4_out ? n18bithalfadder_3_s : 18'bz;  // Controlled_Buffer controlled_buffer_5
  and and_6 (and_6_out, controlunit_1_pcwrite, ~branch_1_bout, controlunit_1_b);  // AND_Gate

  // Notes on the sheet:
  //   contents of rom_1 (hex, n*v repeats v):
  //   2096a 20464 21063 21522 20943 34805 34401 35402 35003 3a002 3a401 3a804 39803 10942 10841 18881
  //   21121 d17f 15142 33ffe 3b403 35ffe
endmodule

module ALU (
  input  [17:0] r1,
  input  [17:0] r2,
  input  [1:0] select,
  output [17:0] out
);

  wire [17:0] and_1_out, n18bithalfadder_1_s, or_1_out, xor_1_out;

  _18bitHalfAdder u_18bithalfadder_1 (.a(r1), .b(r2), .s(n18bithalfadder_1_s));  // open: cout
  assign and_1_out = r1 & r2;  // AND_Gate and_1, 18 bits wide
  assign or_1_out = r1 | r2;  // OR_Gate or_1, 18 bits wide
  assign xor_1_out = r1 ^ r2;  // XOR_Gate xor_1, 18 bits wide
  Multiplexer #(.select(2), .width(18), .enable("false")) multiplexer_1 (
    .in0(n18bithalfadder_1_s), .in1(and_1_out), .in2(or_1_out), .in3(xor_1_out), .out(out), .sel(select));
endmodule

// clk
module ControlUnit (
  input  [17:0] CU_Input,
  input  clk,
  output B,
  output [2:0] nzp,
  output [17:0] JumpExtended,
  output PCread,
  output WE,
  output jumpIns,
  output arithmetic,
  output [17:0] LD_ST_Adress,
  output [1:0] ALUselector,
  output [3:0] SRC2,
  output memRead,
  output memWrite,
  output [3:0] SRC1,
  output [3:0] DST,
  output PCwrite,
  output [17:0] immExtendedB,
  output immediate,
  output [17:0] immExtendedArithmetic
);

  wire and_1_out, decoder_1_out0, decoder_1_out1, decoder_1_out2, decoder_1_out3, decoder_1_out4,
       decoder_1_out5, decoder_1_out6, decoder_1_out8, decoder_1_out9, decoder_1_out10, decoder_1_out11,
       decoder_1_out14, decoder_1_out15, not_1_out, or_1_out, register_1_q;
  wire [3:0] counter_1_q;

  Multiplexer #(.width(4), .enable("false")) multiplexer_1 (
    .in0(4'b0000), .in1(4'b1111), .out(JumpExtended[17:14]), .sel(CU_Input[13]));
  Multiplexer #(.width(12), .enable("false")) multiplexer_2 (
    .in0({12{1'b0}}), .in1({12{1'b1}}), .out(immExtendedB[17:6]), .sel(CU_Input[5]));
  Multiplexer #(.width(13), .enable("false")) multiplexer_3 (
    .in0({13{1'b0}}), .in1({13{1'b1}}), .out(immExtendedArithmetic[17:5]), .sel(CU_Input[4]));
  Counter #(.width(4), .max('hf)) counter_1 (
    .load(decoder_1_out1), .D(CU_Input[17:14]), .count(or_1_out), .Q(counter_1_q), .clk(clk), .clr(and_1_out));  // open: carry
  not not_1 (not_1_out, or_1_out);
  and and_1 (and_1_out, not_1_out, register_1_q);
  Register #(.width(1)) register_1 (.D(PCwrite), .en(1'b1), .Q(register_1_q), .clk(clk));  // open: clr
  Decoder #(.select(4), .enable("false")) decoder_1 (
    .out0(decoder_1_out0), .out1(decoder_1_out1), .out2(decoder_1_out2), .out3(decoder_1_out3),
    .out4(decoder_1_out4), .out5(decoder_1_out5), .out6(decoder_1_out6), .out8(decoder_1_out8),
    .out9(decoder_1_out9), .out10(decoder_1_out10), .out11(decoder_1_out11), .out12(jumpIns),
    .out13(memWrite), .out14(decoder_1_out14), .out15(decoder_1_out15), .sel(counter_1_q));  // open: out7
  or or_1 (or_1_out, decoder_1_out14, decoder_1_out0);
  or or_2 (nzp[2], decoder_1_out5, decoder_1_out3);
  or or_3 (nzp[1], decoder_1_out2, decoder_1_out5, decoder_1_out6);
  or or_4 (nzp[0], decoder_1_out6, decoder_1_out4);
  or or_5 (arithmetic, decoder_1_out8, decoder_1_out9, decoder_1_out10, decoder_1_out11);
  or or_6 (ALUselector[0], decoder_1_out11, decoder_1_out9);
  or or_7 (ALUselector[1], decoder_1_out10, decoder_1_out11);
  or or_8 (PCwrite, decoder_1_out15, jumpIns, decoder_1_out11, decoder_1_out10, decoder_1_out9, decoder_1_out8, memWrite, decoder_1_out2, B);
  or or_9 (B, nzp[2], nzp[1], nzp[0]);
  or or_10 (memRead, decoder_1_out14, decoder_1_out15);
  or or_11 (WE, arithmetic, decoder_1_out14);

  assign DST = CU_Input[13:10];
  assign immediate = CU_Input[5];
  assign immExtendedArithmetic[4:0] = CU_Input[4:0];
  assign immExtendedB[5:0] = CU_Input[5:0];
  assign JumpExtended[13:0] = CU_Input[13:0];
  assign LD_ST_Adress = {{8{1'b0}}, CU_Input[9:0]};
  assign PCread = 1'b1;
  assign SRC1 = CU_Input[9:6];
  assign SRC2 = CU_Input[3:0];

  // Notes on the sheet:
  //   B
  //   ADD
  //   AND
  //   OR
  //   XOR
  //   JUMP
  //   ST
  //   LD1
  //   LD2
endmodule

module branch (
  input  [2:0] nzp,
  input  [17:0] op1,
  input  [17:0] op2,
  output Bout
);

  wire and_1_out, and_2_out, and_3_out, n18bitcomperator_1_eq_out, n18bitcomperator_1_gt_out,
       n18bitcomperator_1_lt_out;

  _18bitComperator u_18bitcomperator_1 (
    .a(op1), .b(op2), .gt_out(n18bitcomperator_1_gt_out), .eq_out(n18bitcomperator_1_eq_out),
    .lt_out(n18bitcomperator_1_lt_out));
  and and_1 (and_1_out, nzp[0], n18bitcomperator_1_gt_out);
  and and_2 (and_2_out, nzp[1], n18bitcomperator_1_eq_out);
  and and_3 (and_3_out, nzp[2], n18bitcomperator_1_lt_out);
  or or_1 (Bout, and_1_out, and_2_out, and_3_out);
endmodule

module registerFile (
  input  [3:0] src1,
  input  [3:0] src2,
  input  [17:0] in_3,
  input  [3:0] dest,
  input  clk,
  input  WE,
  output [17:0] out_7,
  output [17:0] out_8
);

  wire and_1_out, and_2_out, and_3_out, and_4_out, and_5_out, and_6_out, and_7_out, and_8_out, and_9_out,
       and_10_out, and_11_out, and_12_out, and_13_out, and_14_out, and_15_out, and_16_out, decoder_1_out0,
       decoder_1_out1, decoder_1_out2, decoder_1_out3, decoder_1_out4, decoder_1_out5, decoder_1_out6,
       decoder_1_out7, decoder_1_out8, decoder_1_out9, decoder_1_out10, decoder_1_out11, decoder_1_out12,
       decoder_1_out13, decoder_1_out14, decoder_1_out15, decoder_2_out0, decoder_2_out1, decoder_2_out2,
       decoder_2_out3, decoder_2_out4, decoder_2_out5, decoder_2_out6, decoder_2_out7, decoder_2_out8,
       decoder_2_out9, decoder_2_out10, decoder_2_out11, decoder_2_out12, decoder_2_out13, decoder_2_out14,
       decoder_2_out15, decoder_3_out0, decoder_3_out1, decoder_3_out2, decoder_3_out3, decoder_3_out4,
       decoder_3_out5, decoder_3_out6, decoder_3_out7, decoder_3_out8, decoder_3_out9, decoder_3_out10,
       decoder_3_out11, decoder_3_out12, decoder_3_out13, decoder_3_out14, decoder_3_out15;
  wire [17:0] register_1_q, register_2_q, register_3_q, register_4_q, register_5_q, register_6_q,
       register_7_q, register_8_q, register_9_q, register_10_q, register_11_q, register_12_q, register_13_q,
       register_14_q, register_15_q, register_16_q;

  Decoder #(.select(4), .enable("false")) decoder_1 (
    .out0(decoder_1_out0), .out1(decoder_1_out1), .out2(decoder_1_out2), .out3(decoder_1_out3),
    .out4(decoder_1_out4), .out5(decoder_1_out5), .out6(decoder_1_out6), .out7(decoder_1_out7),
    .out8(decoder_1_out8), .out9(decoder_1_out9), .out10(decoder_1_out10), .out11(decoder_1_out11),
    .out12(decoder_1_out12), .out13(decoder_1_out13), .out14(decoder_1_out14), .out15(decoder_1_out15),
    .sel(src2));
  Decoder #(.select(4), .enable("false")) decoder_2 (
    .out0(decoder_2_out0), .out1(decoder_2_out1), .out2(decoder_2_out2), .out3(decoder_2_out3),
    .out4(decoder_2_out4), .out5(decoder_2_out5), .out6(decoder_2_out6), .out7(decoder_2_out7),
    .out8(decoder_2_out8), .out9(decoder_2_out9), .out10(decoder_2_out10), .out11(decoder_2_out11),
    .out12(decoder_2_out12), .out13(decoder_2_out13), .out14(decoder_2_out14), .out15(decoder_2_out15),
    .sel(src1));
  Decoder #(.select(4), .enable("false")) decoder_3 (
    .out0(decoder_3_out0), .out1(decoder_3_out1), .out2(decoder_3_out2), .out3(decoder_3_out3),
    .out4(decoder_3_out4), .out5(decoder_3_out5), .out6(decoder_3_out6), .out7(decoder_3_out7),
    .out8(decoder_3_out8), .out9(decoder_3_out9), .out10(decoder_3_out10), .out11(decoder_3_out11),
    .out12(decoder_3_out12), .out13(decoder_3_out13), .out14(decoder_3_out14), .out15(decoder_3_out15),
    .sel(dest));
  and and_1 (and_1_out, decoder_3_out0, WE);
  and and_2 (and_2_out, decoder_3_out1, WE);
  and and_3 (and_3_out, decoder_3_out2, WE);
  and and_4 (and_4_out, decoder_3_out3, WE);
  and and_5 (and_5_out, decoder_3_out4, WE);
  and and_6 (and_6_out, decoder_3_out5, WE);
  and and_7 (and_7_out, decoder_3_out6, WE);
  and and_8 (and_8_out, decoder_3_out7, WE);
  and and_9 (and_9_out, decoder_3_out8, WE);
  and and_10 (and_10_out, decoder_3_out9, WE);
  and and_11 (and_11_out, decoder_3_out10, WE);
  and and_12 (and_12_out, decoder_3_out11, WE);
  and and_13 (and_13_out, decoder_3_out12, WE);
  and and_14 (and_14_out, decoder_3_out13, WE);
  and and_15 (and_15_out, decoder_3_out14, WE);
  and and_16 (and_16_out, decoder_3_out15, WE);
  Register #(.width(18)) register_1 (.D(in_3), .en(and_1_out), .Q(register_1_q), .clk(clk), .clr(1'b0));
  Register #(.width(18)) register_2 (.D(in_3), .en(and_2_out), .Q(register_2_q), .clk(clk), .clr(1'b0));
  Register #(.width(18)) register_3 (.D(in_3), .en(and_3_out), .Q(register_3_q), .clk(clk), .clr(1'b0));
  Register #(.width(18)) register_4 (.D(in_3), .en(and_4_out), .Q(register_4_q), .clk(clk), .clr(1'b0));
  Register #(.width(18)) register_5 (.D(in_3), .en(and_5_out), .Q(register_5_q), .clk(clk), .clr(1'b0));
  Register #(.width(18)) register_6 (.D(in_3), .en(and_6_out), .Q(register_6_q), .clk(clk), .clr(1'b0));
  Register #(.width(18)) register_7 (.D(in_3), .en(and_7_out), .Q(register_7_q), .clk(clk), .clr(1'b0));
  Register #(.width(18)) register_8 (.D(in_3), .en(and_8_out), .Q(register_8_q), .clk(clk), .clr(1'b0));
  Register #(.width(18)) register_9 (.D(in_3), .en(and_9_out), .Q(register_9_q), .clk(clk), .clr(1'b0));
  Register #(.width(18)) register_10 (.D(in_3), .en(and_10_out), .Q(register_10_q), .clk(clk), .clr(1'b0));
  Register #(.width(18)) register_11 (.D(in_3), .en(and_11_out), .Q(register_11_q), .clk(clk), .clr(1'b0));
  Register #(.width(18)) register_12 (.D(in_3), .en(and_12_out), .Q(register_12_q), .clk(clk), .clr(1'b0));
  Register #(.width(18)) register_13 (.D(in_3), .en(and_13_out), .Q(register_13_q), .clk(clk), .clr(1'b0));
  Register #(.width(18)) register_14 (.D(in_3), .en(and_14_out), .Q(register_14_q), .clk(clk), .clr(1'b0));
  Register #(.width(18)) register_15 (.D(in_3), .en(and_15_out), .Q(register_15_q), .clk(clk), .clr(1'b0));
  Register #(.width(18)) register_16 (.D(in_3), .en(and_16_out), .Q(register_16_q), .clk(clk), .clr(1'b0));
  assign out_7 = decoder_2_out0 ? register_1_q : 18'bz;  // Controlled_Buffer controlled_buffer_1
  assign out_7 = decoder_2_out1 ? register_2_q : 18'bz;  // Controlled_Buffer controlled_buffer_2
  assign out_7 = decoder_2_out2 ? register_3_q : 18'bz;  // Controlled_Buffer controlled_buffer_3
  assign out_7 = decoder_2_out3 ? register_4_q : 18'bz;  // Controlled_Buffer controlled_buffer_4
  assign out_7 = decoder_2_out4 ? register_5_q : 18'bz;  // Controlled_Buffer controlled_buffer_5
  assign out_7 = decoder_2_out5 ? register_6_q : 18'bz;  // Controlled_Buffer controlled_buffer_6
  assign out_7 = decoder_2_out6 ? register_7_q : 18'bz;  // Controlled_Buffer controlled_buffer_7
  assign out_7 = decoder_2_out7 ? register_8_q : 18'bz;  // Controlled_Buffer controlled_buffer_8
  assign out_7 = decoder_2_out8 ? register_9_q : 18'bz;  // Controlled_Buffer controlled_buffer_9
  assign out_7 = decoder_2_out9 ? register_10_q : 18'bz;  // Controlled_Buffer controlled_buffer_10
  assign out_7 = decoder_2_out10 ? register_11_q : 18'bz;  // Controlled_Buffer controlled_buffer_11
  assign out_7 = decoder_2_out11 ? register_12_q : 18'bz;  // Controlled_Buffer controlled_buffer_12
  assign out_7 = decoder_2_out12 ? register_13_q : 18'bz;  // Controlled_Buffer controlled_buffer_13
  assign out_7 = decoder_2_out13 ? register_14_q : 18'bz;  // Controlled_Buffer controlled_buffer_14
  assign out_7 = decoder_2_out14 ? register_15_q : 18'bz;  // Controlled_Buffer controlled_buffer_15
  assign out_7 = decoder_2_out15 ? register_16_q : 18'bz;  // Controlled_Buffer controlled_buffer_16
  assign out_8 = decoder_1_out0 ? register_1_q : 18'bz;  // Controlled_Buffer controlled_buffer_17
  assign out_8 = decoder_1_out1 ? register_2_q : 18'bz;  // Controlled_Buffer controlled_buffer_18
  assign out_8 = decoder_1_out2 ? register_3_q : 18'bz;  // Controlled_Buffer controlled_buffer_19
  assign out_8 = decoder_1_out3 ? register_4_q : 18'bz;  // Controlled_Buffer controlled_buffer_20
  assign out_8 = decoder_1_out4 ? register_5_q : 18'bz;  // Controlled_Buffer controlled_buffer_21
  assign out_8 = decoder_1_out5 ? register_6_q : 18'bz;  // Controlled_Buffer controlled_buffer_22
  assign out_8 = decoder_1_out6 ? register_7_q : 18'bz;  // Controlled_Buffer controlled_buffer_23
  assign out_8 = decoder_1_out7 ? register_8_q : 18'bz;  // Controlled_Buffer controlled_buffer_24
  assign out_8 = decoder_1_out8 ? register_9_q : 18'bz;  // Controlled_Buffer controlled_buffer_25
  assign out_8 = decoder_1_out9 ? register_10_q : 18'bz;  // Controlled_Buffer controlled_buffer_26
  assign out_8 = decoder_1_out10 ? register_11_q : 18'bz;  // Controlled_Buffer controlled_buffer_27
  assign out_8 = decoder_1_out11 ? register_12_q : 18'bz;  // Controlled_Buffer controlled_buffer_28
  assign out_8 = decoder_1_out12 ? register_13_q : 18'bz;  // Controlled_Buffer controlled_buffer_29
  assign out_8 = decoder_1_out13 ? register_14_q : 18'bz;  // Controlled_Buffer controlled_buffer_30
  assign out_8 = decoder_1_out14 ? register_15_q : 18'bz;  // Controlled_Buffer controlled_buffer_31
  assign out_8 = decoder_1_out15 ? register_16_q : 18'bz;  // Controlled_Buffer controlled_buffer_32
endmodule

module _1bitFullAdder (
  input  a,
  input  b,
  input  cin,
  output cout,
  output s
);

  wire and_1_out, and_2_out, and_3_out, xor_1_out;

  and and_1 (and_1_out, a, b);
  and and_2 (and_2_out, a, cin);
  and and_3 (and_3_out, b, cin);
  xor xor_1 (xor_1_out, a, cin);
  xor xor_2 (s, xor_1_out, b);
  or or_1 (cout, and_1_out, and_2_out, and_3_out);
endmodule

module _4bitFullAdder (
  input  [3:0] b,
  input  [3:0] a,
  input  cin,
  output cout,
  output [3:0] s
);

  wire n1bitfulladder_1_cout, n1bitfulladder_2_cout, n1bitfulladder_3_cout;

  _1bitFullAdder u_1bitfulladder_1 (.cout(n1bitfulladder_1_cout), .s(s[0]), .a(a[0]), .b(b[0]), .cin(cin));
  _1bitFullAdder u_1bitfulladder_2 (
    .cout(n1bitfulladder_2_cout), .s(s[1]), .a(a[1]), .b(b[1]), .cin(n1bitfulladder_1_cout));
  _1bitFullAdder u_1bitfulladder_3 (
    .cout(n1bitfulladder_3_cout), .s(s[2]), .a(a[2]), .b(b[2]), .cin(n1bitfulladder_2_cout));
  _1bitFullAdder u_1bitfulladder_4 (.cout(cout), .s(s[3]), .a(a[3]), .b(b[3]), .cin(n1bitfulladder_3_cout));
endmodule

module _8bitFullAdder (
  input  [7:0] a,
  input  cin,
  input  [7:0] b,
  output cout,
  output [7:0] s
);

  wire n4bitfulladder_1_cout;

  _4bitFullAdder u_4bitfulladder_1 (.a(a[3:0]), .b(b[3:0]), .s(s[3:0]), .cout(n4bitfulladder_1_cout), .cin(cin));
  _4bitFullAdder u_4bitfulladder_2 (.a(a[7:4]), .b(b[7:4]), .s(s[7:4]), .cout(cout), .cin(n4bitfulladder_1_cout));
endmodule

module _16bitFullAdder (
  input  cin,
  input  [15:0] a,
  input  [15:0] b,
  output cout,
  output [15:0] s
);

  wire n8bitfulladder_1_cout;

  _8bitFullAdder u_8bitfulladder_1 (.a(b[7:0]), .b(a[7:0]), .cin(cin), .cout(n8bitfulladder_1_cout), .s(s[7:0]));
  _8bitFullAdder u_8bitfulladder_2 (.a(b[15:8]), .b(a[15:8]), .cin(n8bitfulladder_1_cout), .cout(cout), .s(s[15:8]));
endmodule

// ADD
module _18bitHalfAdder (
  input  [17:0] a,
  input  [17:0] b,
  output cout,
  output [17:0] s
);

  wire n16bitfulladder_1_cout;

  _16bitFullAdder u_16bitfulladder_1 (.a(b[15:0]), .b(a[15:0]), .cin(1'b0), .cout(n16bitfulladder_1_cout), .s(s[15:0]));
  _2bitFullAdder u_2bitfulladder_1 (
    .b(b[17:16]), .a(a[17:16]), .cin(n16bitfulladder_1_cout), .cout(cout), .s(s[17:16]));
endmodule

module _2bitFullAdder (
  input  cin,
  input  [1:0] b,
  input  [1:0] a,
  output cout,
  output [1:0] s
);

  wire n1bitfulladder_1_cout;

  _1bitFullAdder u_1bitfulladder_1 (.cout(n1bitfulladder_1_cout), .s(s[0]), .a(a[0]), .b(b[0]), .cin(cin));
  _1bitFullAdder u_1bitfulladder_2 (.cout(cout), .s(s[1]), .a(a[1]), .b(b[1]), .cin(n1bitfulladder_1_cout));
endmodule

module _1bitComperator (
  input  gt_in,
  input  eq_in,
  input  a,
  input  b,
  input  lt_in,
  output gt_out,
  output eq_out,
  output lt_out
);

  wire and_1_out, and_2_out, and_3_out, and_4_out, xnor_1_out;

  and and_1 (and_1_out, a, ~b);  // AND_Gate
  and and_2 (and_2_out, ~a, b);  // AND_Gate
  xnor xnor_1 (xnor_1_out, a, b);
  and and_3 (and_3_out, eq_in, and_1_out);
  and and_4 (and_4_out, eq_in, and_2_out);
  and and_5 (eq_out, eq_in, xnor_1_out);
  or or_1 (gt_out, gt_in, and_3_out);
  or or_2 (lt_out, lt_in, and_4_out);
endmodule

module _2bitComperator (
  input  [1:0] a,
  input  [1:0] b,
  input  gt_in,
  input  eq_in,
  input  lt_in,
  output gt_out,
  output eq_out,
  output lt_out
);

  wire n1bitcomperator_1_eq_out, n1bitcomperator_1_gt_out, n1bitcomperator_1_lt_out;

  _1bitComperator u_1bitcomperator_1 (
    .gt_in(gt_in), .eq_in(eq_in), .lt_in(lt_in), .a(a[1]), .b(b[1]), .gt_out(n1bitcomperator_1_gt_out),
    .eq_out(n1bitcomperator_1_eq_out), .lt_out(n1bitcomperator_1_lt_out));
  _1bitComperator u_1bitcomperator_2 (
    .gt_in(n1bitcomperator_1_gt_out), .eq_in(n1bitcomperator_1_eq_out), .lt_in(n1bitcomperator_1_lt_out),
    .a(a[0]), .b(b[0]), .gt_out(gt_out), .eq_out(eq_out), .lt_out(lt_out));
endmodule

module _4bitComperator (
  input  [3:0] in_1,
  input  [3:0] in_2,
  input  gt_in,
  input  eq_in,
  input  lt_in,
  output gt_out,
  output eq_out,
  output lt_out
);

  wire n2bitcomperator_1_eq_out, n2bitcomperator_1_gt_out, n2bitcomperator_1_lt_out;

  _2bitComperator u_2bitcomperator_1 (
    .a(in_1[3:2]), .b(in_2[3:2]), .gt_in(gt_in), .eq_in(eq_in), .lt_in(lt_in),
    .gt_out(n2bitcomperator_1_gt_out), .eq_out(n2bitcomperator_1_eq_out), .lt_out(n2bitcomperator_1_lt_out));
  _2bitComperator u_2bitcomperator_2 (
    .a(in_1[1:0]), .b(in_2[1:0]), .gt_in(n2bitcomperator_1_gt_out), .eq_in(n2bitcomperator_1_eq_out),
    .lt_in(n2bitcomperator_1_lt_out), .gt_out(gt_out), .eq_out(eq_out), .lt_out(lt_out));
endmodule

module _8bitComperator (
  input  [7:0] a,
  input  [7:0] b,
  input  gt_in,
  input  eq_in,
  input  lt_in,
  output gt_out,
  output eq_out,
  output lt_out
);

  wire n4bitcomperator_1_eq_out, n4bitcomperator_1_gt_out, n4bitcomperator_1_lt_out;

  _4bitComperator u_4bitcomperator_1 (
    .in_1(a[7:4]), .in_2(b[7:4]), .gt_in(gt_in), .eq_in(eq_in), .lt_in(lt_in),
    .gt_out(n4bitcomperator_1_gt_out), .eq_out(n4bitcomperator_1_eq_out), .lt_out(n4bitcomperator_1_lt_out));
  _4bitComperator u_4bitcomperator_2 (
    .in_1(a[3:0]), .in_2(b[3:0]), .gt_in(n4bitcomperator_1_gt_out), .eq_in(n4bitcomperator_1_eq_out),
    .lt_in(n4bitcomperator_1_lt_out), .gt_out(gt_out), .eq_out(eq_out), .lt_out(lt_out));
endmodule

module _16bitComperator (
  input  [15:0] a,
  input  [15:0] b,
  input  gt_in,
  input  eq_in,
  input  lt_in,
  output gt_out,
  output eq_out,
  output lt_out
);

  wire n8bitcomperator_1_eq_out, n8bitcomperator_1_gt_out, n8bitcomperator_1_lt_out;

  _8bitComperator u_8bitcomperator_1 (
    .a(a[15:8]), .b(b[15:8]), .gt_in(gt_in), .eq_in(eq_in), .lt_in(lt_in), .gt_out(n8bitcomperator_1_gt_out),
    .eq_out(n8bitcomperator_1_eq_out), .lt_out(n8bitcomperator_1_lt_out));
  _8bitComperator u_8bitcomperator_2 (
    .a(a[7:0]), .b(b[7:0]), .gt_in(n8bitcomperator_1_gt_out), .eq_in(n8bitcomperator_1_eq_out),
    .lt_in(n8bitcomperator_1_lt_out), .gt_out(gt_out), .eq_out(eq_out), .lt_out(lt_out));
endmodule

module _18bitComperator (
  input  [17:0] a,
  input  [17:0] b,
  output gt_out,
  output eq_out,
  output lt_out
);

  wire n1bitcomperator_1_eq_out, n1bitcomperator_1_gt_out, n1bitcomperator_1_lt_out,
       n16bitcomperator_1_eq_out, n16bitcomperator_1_gt_out, n16bitcomperator_1_lt_out;

  _1bitComperator u_1bitcomperator_1 (
    .gt_in(1'b0), .eq_in(1'b1), .lt_in(1'b0), .a(a[17]), .b(b[17]), .gt_out(n1bitcomperator_1_gt_out),
    .eq_out(n1bitcomperator_1_eq_out), .lt_out(n1bitcomperator_1_lt_out));
  _16bitComperator u_16bitcomperator_1 (
    .a(a[17:2]), .b(b[17:2]), .gt_in(n1bitcomperator_1_lt_out), .eq_in(n1bitcomperator_1_eq_out),
    .lt_in(n1bitcomperator_1_gt_out), .gt_out(n16bitcomperator_1_gt_out), .eq_out(n16bitcomperator_1_eq_out),
    .lt_out(n16bitcomperator_1_lt_out));
  _2bitComperator u_2bitcomperator_1 (
    .a(a[1:0]), .b(b[1:0]), .gt_in(n16bitcomperator_1_gt_out), .eq_in(n16bitcomperator_1_eq_out),
    .lt_in(n16bitcomperator_1_lt_out), .gt_out(gt_out), .eq_out(eq_out), .lt_out(lt_out));
endmodule
